# Fritzing sketch Amecite-Tilt-Neopixel (saved by Fritzing 0.9.3b)
breadboards: 1

parts:
  Part1 = Arduino Uno (Rev3)
  S1 = Tilt Switch [package=THT]
  NEOPIXEL1 = Neopixel Strip -- Black (30/m) [part_number=1376]

nets:
  N1: Part1.D2, S1.Pin_2
  N2: Part1.D6_PWM, NEOPIXEL1.Din
  5V: Part1.5V, NEOPIXEL1.+5V
  GND: Part1.GND, S1.Pin_1, NEOPIXEL1.GND

custom parts:
  Neopixel Strip -- Black (30/m): These NeoPixel strips have 30 digitally-addressable pixel LEDs per meter and are very affordable and are only 12.5 mm wide, 10 mm if you remove the strip from the casing.
